// Logisim project ChristophSamuel-JankowiakMatthias.circ as structural Verilog: 8 circuits, main circuit éxécution_d'une_séquence_de_calcul
module addition (
  input  [7:0] A,
  input  [7:0] B,
  output [7:0] S,
  output D
);

  // Probe on A
  // Probe on B
  Adder adder_1 (.a(A), .b(B), .out(S), .cout(D));  // open: cin
  // Probe on S
endmodule

module soustraction (
  input  [7:0] A,
  input  [7:0] B,
  output D,
  output [7:0] S,
  output D_2
);

  wire active, comparator_1_gt;
  wire [7:0] subtractor_1_out, subtractor_2_out;

  // Probe on A
  // Probe on B
  Comparator #(.mode("unsigned")) comparator_1 (.a(A), .b(B), .gt(comparator_1_gt), .lt(active));  // open: eq
  Subtractor subtractor_1 (.a(A), .b(B), .out(subtractor_1_out), .bout(D));  // open: bin
  Subtractor subtractor_2 (.a(B), .b(A), .out(subtractor_2_out), .bout(D_2));  // open: bin
  // Probe on S
  Multiplexer #(.width(8), .disabled(0), .enable("false")) multiplexer_1 (
    .in0(subtractor_1_out), .in1(subtractor_2_out), .out(S), .sel(active));
endmodule

module multiplication (
  input  [7:0] A,
  input  [7:0] B,
  output [7:0] S,
  output D
);

  wire [7:0] multiplier_1_cout;

  // Probe on A
  Multiplier multiplier_1 (.a(A), .b(B), .out(S), .cout(multiplier_1_cout));  // open: cin
  // Probe on B
  // Probe on S
  Comparator comparator_1 (.a(multiplier_1_cout), .b({8{1'b0}}), .gt(D));  // open: eq, lt
endmodule

module division (
  input  [7:0] A,
  input  [7:0] B,
  output [7:0] D,
  output [7:0] S,
  output [7:0] D_2
);

  wire active, comparator_1_gt, comparator_2_lt;
  wire [7:0] adder_1_out, divider_1_out, divider_2_out, not_1_out, R;

  // Probe on A
  // Probe on B
  Comparator comparator_1 (.a(A), .b(B), .gt(comparator_1_gt), .lt(active));  // open: eq
  Divider divider_1 (.a(A), .b(B), .out(divider_1_out), .rem(D));  // open: upper
  Divider divider_2 (.a(B), .b(A), .out(divider_2_out), .rem(D_2));  // open: upper
  Multiplexer #(.width(8), .disabled(0), .enable("false")) multiplexer_1 (
    .in0(divider_1_out), .in1(divider_2_out), .out(R), .sel(active));
  assign not_1_out = ~R;  // NOT_Gate not_1, 8 bits wide
  Multiplexer #(.width(8), .enable("false")) multiplexer_2 (.in0(R), .in1(adder_1_out), .out(S), .sel(comparator_2_lt));
  Adder adder_1 (.a(not_1_out), .b(8'h1), .out(adder_1_out));  // open: cin, cout
  Comparator comparator_2 (.a(R), .b({8{1'b0}}), .lt(comparator_2_lt));  // open: gt, eq
  // Probe on S
endmodule

module \unité_de_calcul  (
  input  [7:0] A,
  input  [7:0] B,
  input  [1:0] \code_d_opération ,
  output [7:0] S,
  output D
);

  wire addition_d, multiplication_d;
  wire [7:0] addition_s, division_s, multiplication_s, soustraction_s;

  // Probe on A
  // Probe on B
  addition addition (.A(A), .B(B), .D(addition_d), .S(addition_s));
  soustraction soustraction (.A(A), .B(B), .S(soustraction_s));  // open: D, D_2
  multiplication multiplication (.A(A), .B(B), .D(multiplication_d), .S(multiplication_s));
  division division (.A(B), .B(A), .S(division_s));  // open: D, D_2
  // Probe on S
  Multiplexer #(.select(2), .width(8), .enable("false")) multiplexer_1 (
    .in0(addition_s), .in1(soustraction_s), .in2(multiplication_s), .in3(division_s), .out(S),
    .sel(\code_d_opération ));
  Multiplexer #(.select(2), .enable("false")) multiplexer_2 (
    .in0(addition_d), .in1(1'b0), .in2(multiplication_d), .in3(1'b0), .out(D), .sel(\code_d_opération ));
endmodule

module \implémentation_d_une_pile  (
  input  [7:0] \entrée_de_données ,
  input  \code_d_opération ,
  input  horloge,
  input  clear,
  input  E,
  output [7:0] \sortie_de_données 
);

  wire controlled_buffer_1_out, not_1_out, not_2_out, not_3_out;
  wire [7:0] controlled_buffer_2_out, counter_1_q;

  // Probe on \entrée_de_données 
  not not_1 (not_1_out, \code_d_opération );
  assign controlled_buffer_1_out = E ? horloge : 1'bz;  // Controlled_Buffer controlled_buffer_1
  assign controlled_buffer_2_out = \code_d_opération  ? \entrée_de_données  : 8'bz;  // Controlled_Buffer controlled_buffer_2
  Counter #(.ongoal("load")) counter_1 (
    .load(not_1_out), .Q(counter_1_q), .clk(controlled_buffer_1_out), .clr(clear));  // open: D, count, carry
  RAM ram_1 (
    .addr(counter_1_q), .data(controlled_buffer_2_out), .clk(controlled_buffer_1_out), .ld(not_2_out),
    .clr(clear));  // open: sel
  not not_2 (not_2_out, \code_d_opération );
  assign \sortie_de_données  = not_3_out ? controlled_buffer_2_out : 8'bz;  // Controlled_Buffer controlled_buffer_3
  not not_3 (not_3_out, \code_d_opération );
  // Probe on \sortie_de_données 

  // Notes on the sheet:
  //   E: pull=up
endmodule

module \éxécution_d_une_séquence_de_calcul  (
);

  wire A, and_3_out, B, C, clock, comparator_2_eq, comparator_3_gt, comparator_4_eq, comparator_4_gt,
       comparator_4_lt, controlled_buffer_1_out, controlled_buffer_5_out, not_1_out, not_2_out, or_2_out,
       \réinitialisation , STOP, \sup_à_1 , \unité_de_calcul_d ;
  wire [1:0] bit_extender_1_out;
  wire [7:0] code, controlled_buffer_2_out, controlled_buffer_3_out, controlled_buffer_4_out, counter,
       multiplexer_1_out, rom_1_data, \Résultat , subtractor_1_out, Valeur_A, Valeur_B;

  Clock u_Clock (.out(clock));
  Button \Réinitialisation_ROM  (.out(\réinitialisation ));
  // Probe on code
  // Probe on Valeur_A
  // Probe on Valeur_B
  // Probe on Valeur_A
  Counter #(.ongoal("load")) counter_1 (
    .Q(counter), .clk(controlled_buffer_1_out), .clr(\réinitialisation ));  // open: load, D, count, carry
  not not_1 (not_1_out, STOP);
  assign controlled_buffer_1_out = not_1_out ? clock : 1'bz;  // Controlled_Buffer controlled_buffer_1
  // Probe on \Résultat 
  Comparator comparator_1 (.a(counter), .b({8{1'b0}}), .gt(\sup_à_1 ), .eq(A));  // open: lt
  ROM rom_1 (.addr(counter), .data(rom_1_data));  // open: sel
  Comparator comparator_2 (.a(code), .b({8{1'b0}}), .eq(comparator_2_eq));  // open: gt, lt
  and and_1 (STOP, comparator_2_eq, comparator_3_gt);
  Comparator comparator_3 (.a(counter), .b(8'h2), .gt(comparator_3_gt));  // open: eq, lt
  Comparator comparator_4 (
    .a(rom_1_data), .b({8{1'b0}}), .gt(comparator_4_gt), .eq(comparator_4_eq), .lt(comparator_4_lt));
  and and_2 (B, \sup_à_1 , comparator_4_gt);
  or or_1 (C, comparator_4_eq, comparator_4_lt);
  or or_2 (or_2_out, A, and_3_out);
  assign controlled_buffer_2_out = or_2_out ? rom_1_data : 8'bz;  // Controlled_Buffer controlled_buffer_2
  assign controlled_buffer_3_out = B ? rom_1_data : 8'bz;  // Controlled_Buffer controlled_buffer_3
  assign controlled_buffer_4_out = C ? rom_1_data : 8'bz;  // Controlled_Buffer controlled_buffer_4
  and and_3 (and_3_out, C, \sup_à_1 );
  Register B_2 (.D(controlled_buffer_3_out), .Q(Valeur_B), .clk(clock), .clr(\réinitialisation ));  // open: en
  Register \code_opération_2  (
    .D(controlled_buffer_4_out), .Q(code), .clk(clock), .clr(\réinitialisation ));  // open: en
  Multiplexer #(.width(8), .enable("false")) multiplexer_1 (
    .in0(controlled_buffer_2_out), .in1(\Résultat ), .out(multiplexer_1_out), .sel(and_3_out));
  Register A_2 (
    .D(multiplexer_1_out), .Q(Valeur_A), .clk(controlled_buffer_5_out), .clr(\réinitialisation ));  // open: en
  assign controlled_buffer_5_out = not_2_out ? clock : 1'bz;  // Controlled_Buffer controlled_buffer_5
  not not_2 (not_2_out, STOP);
  Subtractor subtractor_1 (.a(code), .b(8'h1), .out(subtractor_1_out));  // open: bin, bout
  \unité_de_calcul  \unité_de_calcul  (
    .A(Valeur_A), .B(Valeur_B), .\code_d_opération (bit_extender_1_out), .S(\Résultat ),
    .D(\unité_de_calcul_d ));
  Bit_Extender #(.out_width(2)) bit_extender_1 (.in(subtractor_1_out), .out(bit_extender_1_out));
  LED #(.active("false")) \Diode_de_débordement  (.in(\unité_de_calcul_d ));

  // Notes on the sheet:
  //   contents of rom_1 (hex, n*v repeats v):
  //   5 83 12 81 17 84 2 82 22
endmodule

module \test_séquence_pile  (
  input  in_1,
  input  in_2
);

  wire A, and_1_out, B, C, clock, comparator_1_gt, comparator_1_lt, comparator_2_eq, comparator_4_eq,
       comparator_5_eq, comparator_6_eq, comparator_7_eq, comparator_8_eq, comparator_9_eq, comparator_9_gt,
       comparator_9_lt, controlled_buffer_1_out, diff3, not_1_out, not_2_out, not_3_out, or_4_out,
       \réinitialisation , STOP, te, \unité_de_calcul_d ;
  wire [1:0] bit_extender_1_out;
  wire [7:0] code, controlled_buffer_2_out, controlled_buffer_3_out, controlled_buffer_4_out, counter,
       multiplexer_1_out, \Résultat , subtractor_1_out, Valeur_A, Valeur_B, x, z;

  Clock u_Clock (.out(clock));
  Button \Réinitialisation_ROM  (.out(\réinitialisation ));
  not not_1 (not_1_out, STOP);
  assign controlled_buffer_1_out = not_1_out ? clock : 1'bz;  // Controlled_Buffer controlled_buffer_1
  // Probe on code
  Counter #(.ongoal("load")) counter_1 (
    .Q(counter), .clk(controlled_buffer_1_out), .clr(\réinitialisation ));  // open: load, D, count, carry
  // Probe on Valeur_A
  Comparator comparator_1 (.a(counter), .b({8{1'b0}}), .gt(comparator_1_gt), .lt(comparator_1_lt));  // open: eq
  not not_2 (not_2_out, in_2);
  // Probe on Valeur_B
  // Probe on Valeur_A
  Comparator comparator_2 (.a(z), .b({8{1'b0}}), .eq(comparator_2_eq));  // open: gt, lt
  and and_1 (and_1_out, in_2, te);
  and and_2 (diff3, comparator_1_gt, comparator_1_lt);
  // Probe on \Résultat 
  or or_1 (STOP, comparator_2_eq, and_1_out);
  ROM rom_1 (.addr(counter), .data(z));  // open: sel
  // Probe on z
  Comparator comparator_3 (.a(x), .b(8'hc), .eq(A));  // open: gt, lt
  Comparator comparator_4 (.a(x), .b(8'hc), .eq(comparator_4_eq));  // open: gt, lt
  \implémentation_d_une_pile  Pile (
    .\code_d_opération (not_2_out), .horloge(clock), .E(in_1), .\entrée_de_données (z),
    .\sortie_de_données (x), .clear(\réinitialisation ));
  Comparator comparator_5 (.a(counter), .b(8'h4), .eq(comparator_5_eq));  // open: gt, lt
  Comparator comparator_6 (.a(counter), .b(8'h5), .eq(comparator_6_eq));  // open: gt, lt
  Comparator comparator_7 (.a(counter), .b(8'h7), .eq(comparator_7_eq));  // open: gt, lt
  Comparator comparator_8 (.a(counter), .b(8'h9), .eq(comparator_8_eq));  // open: gt, lt
  not not_3 (not_3_out, comparator_4_eq);
  Comparator comparator_9 (.a(x), .b({8{1'b0}}), .gt(comparator_9_gt), .eq(comparator_9_eq), .lt(comparator_9_lt));
  or or_2 (te, comparator_5_eq, comparator_6_eq, comparator_7_eq, comparator_8_eq);
  and and_3 (B, not_3_out, comparator_9_gt);
  or or_3 (C, comparator_9_eq, comparator_9_lt);
  // Probe on x
  or or_4 (or_4_out, A, C);
  assign controlled_buffer_2_out = or_4_out ? x : 8'bz;  // Controlled_Buffer controlled_buffer_2
  assign controlled_buffer_3_out = B ? x : 8'bz;  // Controlled_Buffer controlled_buffer_3
  assign controlled_buffer_4_out = C ? x : 8'bz;  // Controlled_Buffer controlled_buffer_4
  Register B_2 (.D(controlled_buffer_3_out), .Q(Valeur_B), .clk(clock), .clr(\réinitialisation ));  // open: en
  Register u_code (.D(controlled_buffer_4_out), .Q(code), .clk(clock), .clr(\réinitialisation ));  // open: en
  Multiplexer #(.width(8), .enable("false")) multiplexer_1 (
    .in0(controlled_buffer_2_out), .in1(\Résultat ), .out(multiplexer_1_out), .sel(C));
  Register A_2 (.D(multiplexer_1_out), .Q(Valeur_A), .clk(clock), .clr(\réinitialisation ));  // open: en
  // NOT_Gate not_4 has open pins: in=STOP, out=open
  Subtractor subtractor_1 (.a(code), .b(8'h1), .out(subtractor_1_out));  // open: bin, bout
  Bit_Extender #(.out_width(2)) bit_extender_1 (.in(subtractor_1_out), .out(bit_extender_1_out));
  \unité_de_calcul  \unité_de_calcul  (
    .A(Valeur_A), .B(Valeur_B), .\code_d_opération (bit_extender_1_out), .S(\Résultat ),
    .D(\unité_de_calcul_d ));
  LED #(.active("false")) \Diode_de_débordement  (.in(\unité_de_calcul_d ));

  // Other names for the same wires on the sheet: active = in_1

  // Notes on the sheet:
  //   contents of rom_1 (hex, n*v repeats v):
  //   11 5 c 83 81 2 84 16 82
endmodule
